// Logisim project Avance Practica4.circ as structural Verilog: 5 circuits, main circuit main
module main (
  input  C_in,
  input  A,
  input  B,
  output Suma,
  output Carry_Out
);

  wire and_1_out, and_2_out, xor_1_out;

  xor xor_1 (xor_1_out, A, B);
  and and_1 (and_1_out, A, B);
  xor xor_2 (Suma, C_in, xor_1_out);
  and and_2 (and_2_out, C_in, xor_1_out);
  or or_1 (Carry_Out, and_2_out, and_1_out);

  // Notes on the sheet:
  //   Full Adder Ejercicio 1
endmodule

module Ejercicio_2 (
  input  [7:0] in_1,
  input  C,
  input  [7:0] in_3,
  output [7:0] out_4
);

  wire main_1_carry_out, main_2_carry_out, main_3_carry_out, main_4_carry_out, main_5_carry_out,
       main_6_carry_out, main_7_carry_out;

  main main_1 (.C_in(C), .A(in_1[0]), .B(in_3[0]), .Suma(out_4[0]), .Carry_Out(main_1_carry_out));
  main main_2 (.C_in(main_1_carry_out), .A(in_1[1]), .B(in_3[1]), .Suma(out_4[1]), .Carry_Out(main_2_carry_out));
  main main_3 (.C_in(main_2_carry_out), .A(in_1[2]), .B(in_3[2]), .Suma(out_4[2]), .Carry_Out(main_3_carry_out));
  main main_4 (.C_in(main_3_carry_out), .A(in_1[3]), .B(in_3[3]), .Suma(out_4[3]), .Carry_Out(main_4_carry_out));
  main main_5 (.C_in(main_4_carry_out), .A(in_1[4]), .B(in_3[4]), .Suma(out_4[4]), .Carry_Out(main_5_carry_out));
  main main_6 (.C_in(main_5_carry_out), .A(in_1[5]), .B(in_3[5]), .Suma(out_4[5]), .Carry_Out(main_6_carry_out));
  main main_7 (.C_in(main_6_carry_out), .A(in_1[6]), .B(in_3[6]), .Suma(out_4[6]), .Carry_Out(main_7_carry_out));
  main main_8 (.C_in(main_7_carry_out), .A(in_1[7]), .B(in_3[7]), .Suma(out_4[7]));  // open: Carry_Out

  // Notes on the sheet:
  //   A
  //   B
  //   Sumador de 8bits
endmodule

module Ejercicio_3 (
  input  in_1,
  input  [7:0] in_2,
  input  [7:0] in_3,
  input  in_4,
  output [7:0] out_5
);

  wire [7:0] ejercicio_2_out_4, restador_8bits_out_4;

  Ejercicio_2 ejercicio_2 (.in_1(in_2), .C(in_1), .in_3(in_3), .out_4(ejercicio_2_out_4));
  restador_8bits restador_8bits (.in_1(in_2), .C(in_1), .in_3(in_3), .out_4(restador_8bits_out_4));
  Multiplexer #(.width(8), .enable("false")) multiplexer_1 (
    .in0(ejercicio_2_out_4), .in1(restador_8bits_out_4), .out(out_5), .sel(in_4));
endmodule

module restador (
  input  C_in,
  input  A,
  input  B,
  output Resta,
  output Carry_Out
);

  wire and_1_out, and_2_out, not_1_out, xor_1_out;

  not not_1 (not_1_out, A);
  xor xor_1 (xor_1_out, A, B);
  and and_1 (and_1_out, not_1_out, B);
  xor xor_2 (Resta, C_in, xor_1_out);
  and and_2 (and_2_out, C_in, xor_1_out);
  or or_1 (Carry_Out, and_2_out, and_1_out);
endmodule

module restador_8bits (
  input  [7:0] in_1,
  input  C,
  input  [7:0] in_3,
  output [7:0] out_4
);

  wire restador_1_carry_out, restador_2_carry_out, restador_3_carry_out, restador_4_carry_out,
       restador_5_carry_out, restador_6_carry_out, restador_7_carry_out;

  restador restador_1 (.C_in(C), .A(in_1[0]), .B(in_3[0]), .Resta(out_4[0]), .Carry_Out(restador_1_carry_out));
  restador restador_2 (
    .C_in(restador_1_carry_out), .A(in_1[1]), .B(in_3[1]), .Resta(out_4[1]), .Carry_Out(restador_2_carry_out));
  restador restador_3 (
    .C_in(restador_2_carry_out), .A(in_1[2]), .B(in_3[2]), .Resta(out_4[2]), .Carry_Out(restador_3_carry_out));
  restador restador_4 (
    .C_in(restador_3_carry_out), .A(in_1[3]), .B(in_3[3]), .Resta(out_4[3]), .Carry_Out(restador_4_carry_out));
  restador restador_5 (
    .C_in(restador_4_carry_out), .A(in_1[4]), .B(in_3[4]), .Resta(out_4[4]), .Carry_Out(restador_5_carry_out));
  restador restador_6 (
    .C_in(restador_5_carry_out), .A(in_1[5]), .B(in_3[5]), .Resta(out_4[5]), .Carry_Out(restador_6_carry_out));
  restador restador_7 (
    .C_in(restador_6_carry_out), .A(in_1[6]), .B(in_3[6]), .Resta(out_4[6]), .Carry_Out(restador_7_carry_out));
  restador restador_8 (.C_in(restador_7_carry_out), .A(in_1[7]), .B(in_3[7]), .Resta(out_4[7]));  // open: Carry_Out

  // Notes on the sheet:
  //   A
  //   B
  //   Restador de 8bits
endmodule
