// Logisim project practica5.circ as structural Verilog: 3 circuits, main circuit Ejercicio 1
module Ejercicio_1 (
  input  In,
  input  Dummy
);

  wire and_1_out, and_2_out, and_3_out, clock_1_out, not_1_out, not_2_out, not_3_out;
  wire [1:0] s_r_ff_2_q;

  not not_1 (not_1_out, s_r_ff_2_q[1]);
  not not_2 (not_2_out, s_r_ff_2_q[0]);
  not not_3 (not_3_out, In);
  and and_1 (and_1_out, not_3_out, s_r_ff_2_q[0], not_1_out);
  and and_2 (and_2_out, not_3_out, s_r_ff_2_q[0], s_r_ff_2_q[1]);
  and and_3 (and_3_out, not_3_out, not_2_out);
  Clock clock_1 (.out(clock_1_out));
  S_R_Flip_Flop s_r_ff_1 (
    .S(and_1_out), .clk(clock_1_out), .R(and_2_out), .Q(s_r_ff_2_q[1]));  // open: Qn, preset, reset, en
  S_R_Flip_Flop s_r_ff_2 (
    .S(and_3_out), .clk(clock_1_out), .R(s_r_ff_2_q[0]), .Q(s_r_ff_2_q[0]));  // open: Qn, preset, reset, en
  Hex_Digit_Display hex_digit_display_1 (.value({{2{Dummy}}, s_r_ff_2_q}));  // open: dp

  // Notes on the sheet:
  //   So
  //   SL
  //   SoR
  //   SLS
  //   SoS
  //   SLR
  //   So
  //   SL
endmodule

module Ejercicio_2 (
  input  [7:0] in_1,
  output [7:0] out_2
);

  wire clock_1_out;

  Clock clock_1 (.out(clock_1_out));
  D_Flip_Flop d_ff_1 (.clk(clock_1_out), .D(in_1[7]), .Q(out_2[7]));  // open: Qn, preset, en, reset
  D_Flip_Flop d_ff_2 (.clk(clock_1_out), .D(in_1[6]), .Q(out_2[6]));  // open: Qn, preset, en, reset
  D_Flip_Flop d_ff_3 (.clk(clock_1_out), .D(in_1[5]), .Q(out_2[5]));  // open: Qn, preset, en, reset
  D_Flip_Flop d_ff_4 (.clk(clock_1_out), .D(in_1[4]), .Q(out_2[4]));  // open: Qn, preset, en, reset
  D_Flip_Flop d_ff_5 (.clk(clock_1_out), .D(in_1[3]), .Q(out_2[3]));  // open: Qn, preset, en, reset
  D_Flip_Flop d_ff_6 (.clk(clock_1_out), .D(in_1[2]), .Q(out_2[2]));  // open: Qn, preset, en, reset
  D_Flip_Flop d_ff_7 (.clk(clock_1_out), .D(in_1[1]), .Q(out_2[1]));  // open: Qn, preset, en, reset
  D_Flip_Flop d_ff_8 (.clk(clock_1_out), .D(in_1[0]), .Q(out_2[0]));  // open: Qn, preset, en, reset

  // Notes on the sheet:
  //   Registro en paralelo (PIPO)
endmodule

module Ejercicio_3 (
  input  in_1,
  output [7:0] out_2
);

  wire clock_1_out;

  Clock clock_1 (.out(clock_1_out));
  D_Flip_Flop d_ff_1 (.clk(clock_1_out), .D(in_1), .Q(out_2[7]));  // open: Qn, preset, en, reset
  D_Flip_Flop d_ff_2 (.clk(clock_1_out), .D(out_2[7]), .Q(out_2[6]));  // open: Qn, preset, en, reset
  D_Flip_Flop d_ff_3 (.clk(clock_1_out), .D(out_2[6]), .Q(out_2[5]));  // open: Qn, preset, en, reset
  D_Flip_Flop d_ff_4 (.clk(clock_1_out), .D(out_2[5]), .Q(out_2[4]));  // open: Qn, preset, en, reset
  D_Flip_Flop d_ff_5 (.clk(clock_1_out), .D(out_2[4]), .Q(out_2[3]));  // open: Qn, preset, en, reset
  D_Flip_Flop d_ff_6 (.clk(clock_1_out), .D(out_2[3]), .Q(out_2[2]));  // open: Qn, preset, en, reset
  D_Flip_Flop d_ff_7 (.clk(clock_1_out), .D(out_2[2]), .Q(out_2[1]));  // open: Qn, preset, en, reset
  D_Flip_Flop d_ff_8 (.clk(clock_1_out), .D(out_2[1]), .Q(out_2[0]));  // open: Qn, preset, en, reset

  // Notes on the sheet:
  //   Shift register (Registro de desplazamiento)
endmodule
